// Logisim project risc_cpu_simulation.circ as structural Verilog: 2 circuits, main circuit main
module main (
);

  PC_v1 pc_v1_1 ();  // open: PC_In, PC_Select, CLK, Reset, PC_Out
endmodule

module PC_v1 (
  input  [31:0] PC_In,
  input  PC_Select,
  input  CLK,
  input  Reset,
  output [31:0] PC_Out
);

  wire [31:0] adder_1_out, multiplexer_1_out;

  Adder #(.width(32)) adder_1 (.a(PC_Out), .b(32'h4), .out(adder_1_out));  // open: cin, cout
  Multiplexer #(.width(32)) multiplexer_1 (.in0(adder_1_out), .in1(PC_In), .out(multiplexer_1_out), .sel(PC_Select));
  Register #(.width(32)) register_1 (.D(multiplexer_1_out), .en(1'b1), .clk(CLK), .Q(PC_Out), .clr(Reset));
endmodule
